// Logisim project luiz_gabriel_antunes_sena_novo.circ as structural Verilog: 11 circuits, main circuit main
module main (
  input  in_1,
  input  in_2,
  input  in_3
);

  wire R1_p1, R1_p4, R2_p4, R3_p4;
  wire [7:0] controlled_buffer_1_out, R0_d, R1_p3, R2_p3, R3_p3, register_1_q, register_3_q, ula_1_s;

  // Probe on controlled_buffer_1_out
  Register register_1 (.D(controlled_buffer_1_out), .Q(register_1_q), .clk(in_2));  // open: en, clr
  assign controlled_buffer_1_out = R1_p1 ? R0_d : 8'bz;  // Controlled_Buffer controlled_buffer_1
  registrador_set_enable R0 (.i(controlled_buffer_1_out), .d(R0_d));  // open: set, enable
  ula ula_1 (
    .A(register_1_q), .B(controlled_buffer_1_out), .s(ula_1_s));  // open: op, b_1, c_in, c_out, a_maior, iguais, zero
  assign controlled_buffer_1_out = R1_p4 ? R1_p3 : 8'bz;  // Controlled_Buffer controlled_buffer_2
  // registrador_set_enable R1: pin names not known; wires that end beside it: R1_p1, controlled_buffer_1_out, R1_p3, R1_p4
  Register register_2 (.D(ula_1_s), .Q(controlled_buffer_1_out));  // open: en, clk, clr
  assign controlled_buffer_1_out = R2_p4 ? R2_p3 : 8'bz;  // Controlled_Buffer controlled_buffer_3
  // registrador_set_enable R2: pin names not known; wires that end beside it: R1_p4, controlled_buffer_1_out, R2_p3, R2_p4
  // registrador_set_enable R3: pin names not known; wires that end beside it: R2_p4, controlled_buffer_1_out, R3_p3, R3_p4
  assign controlled_buffer_1_out = R3_p4 ? R3_p3 : 8'bz;  // Controlled_Buffer controlled_buffer_4
  RAM #(.databus("bidir")) ram_1 (.addr(register_3_q));  // open: we, oe, clk, data
  Register register_3 (.D(controlled_buffer_1_out), .Q(register_3_q));  // open: en, clk, clr
endmodule

module soma_1b (
  input  c_in,
  input  a,
  input  b,
  output s,
  output c_out
);

  wire and_1_out, and_2_out, and_3_out, xor_1_out;

  xor xor_1 (xor_1_out, a, b);
  and and_1 (and_1_out, a, b);
  and and_2 (and_2_out, c_in, a);
  and and_3 (and_3_out, c_in, b);
  xor xor_2 (s, xor_1_out, c_in);
  or or_1 (c_out, and_1_out, and_2_out, and_3_out);
endmodule

module soma_8b (
  input  [7:0] A,
  input  c_in,
  input  [7:0] B,
  output [7:0] S,
  output c_out
);

  wire soma_1b_1_c_out, soma_1b_2_c_out, soma_1b_3_c_out, soma_1b_4_c_out, soma_1b_5_c_out, soma_1b_6_c_out,
       soma_1b_7_c_out;

  soma_1b soma_1b_1 (.a(A[0]), .b(B[0]), .c_in(c_in), .c_out(soma_1b_1_c_out), .s(S[0]));
  soma_1b soma_1b_2 (.a(A[1]), .b(B[1]), .c_in(soma_1b_1_c_out), .c_out(soma_1b_2_c_out), .s(S[1]));
  soma_1b soma_1b_3 (.a(A[2]), .b(B[2]), .c_in(soma_1b_2_c_out), .c_out(soma_1b_3_c_out), .s(S[2]));
  soma_1b soma_1b_4 (.a(A[3]), .b(B[3]), .c_in(soma_1b_3_c_out), .c_out(soma_1b_4_c_out), .s(S[3]));
  soma_1b soma_1b_5 (.a(A[4]), .b(B[4]), .c_in(soma_1b_4_c_out), .c_out(soma_1b_5_c_out), .s(S[4]));
  soma_1b soma_1b_6 (.a(A[5]), .b(B[5]), .c_in(soma_1b_5_c_out), .c_out(soma_1b_6_c_out), .s(S[5]));
  soma_1b soma_1b_7 (.a(A[6]), .b(B[6]), .c_in(soma_1b_6_c_out), .c_out(soma_1b_7_c_out), .s(S[6]));
  soma_1b soma_1b_8 (.a(A[7]), .b(B[7]), .c_in(soma_1b_7_c_out), .c_out(c_out), .s(S[7]));
endmodule

module memoria_1b (
  input  i,
  input  s,
  output d
);

  wire nand_1_out, nand_2_out, nand_4_out;

  nand nand_1 (nand_1_out, i, s);
  nand nand_2 (nand_2_out, nand_1_out, s);
  nand nand_3 (d, nand_1_out, nand_4_out);
  nand nand_4 (nand_4_out, d, nand_2_out);
endmodule

module memoria_8b (
  input  [7:0] i,
  input  s,
  output [7:0] d
);

  memoria_1b memoria_1b_1 (.i(i[0]), .s(s), .d(d[0]));
  memoria_1b memoria_1b_2 (.i(i[1]), .s(s), .d(d[1]));
  memoria_1b memoria_1b_3 (.i(i[2]), .s(s), .d(d[2]));
  memoria_1b memoria_1b_4 (.i(i[3]), .s(s), .d(d[3]));
  memoria_1b memoria_1b_5 (.i(i[4]), .s(s), .d(d[4]));
  memoria_1b memoria_1b_6 (.i(i[5]), .s(s), .d(d[5]));
  memoria_1b memoria_1b_7 (.i(i[6]), .s(s), .d(d[6]));
  memoria_1b memoria_1b_8 (.i(i[7]), .s(s), .d(d[7]));
endmodule

module registrador_set_enable (
  input  [7:0] i,
  input  set,
  input  enable,
  output [7:0] d
);

  wire [7:0] bit_extender_1_out, memoria_8b_1_d;

  memoria_8b memoria_8b_1 (.i(i), .s(set), .d(memoria_8b_1_d));
  assign bit_extender_1_out = {{7{enable}}, enable};  // Bit_Extender bit_extender_1
  assign d = memoria_8b_1_d & bit_extender_1_out;  // AND_Gate and_1, 8 bits wide
endmodule

module ula (
  input  [2:0] op,
  input  [7:0] A,
  input  b_1,
  input  [7:0] B,
  input  c_in,
  output c_out,
  output [7:0] s,
  output a_maior,
  output iguais,
  output zero
);

  wire and_2_out, shift_l_1_c_out, shift_r_1_c_out, soma_8b_1_c_out;
  wire [7:0] and_1_out, not_1_out, or_1_out, shift_l_1_d, shift_r_1_d, soma_8b_1_s, xor_1_out;

  assign not_1_out = ~B;  // NOT_Gate not_1, 8 bits wide
  soma_8b soma_8b_1 (.A(A), .B(B), .c_in(and_2_out), .c_out(soma_8b_1_c_out), .S(soma_8b_1_s));
  shift_r shift_r_1 (.i(B), .c_in(and_2_out), .c_out(shift_r_1_c_out), .d(shift_r_1_d));
  shift_l shift_l_1 (.i(B), .c_in(and_2_out), .c_out(shift_l_1_c_out), .d(shift_l_1_d));
  assign and_1_out = A & B;  // AND_Gate and_1, 8 bits wide
  assign or_1_out = A | B;  // OR_Gate or_1, 8 bits wide
  assign xor_1_out = A ^ B;  // XOR_Gate xor_1, 8 bits wide
  comp_8b comp_8b_1 (.A(A), .B(B), .a_maior(a_maior), .iguais(iguais));  // open: C
  Multiplexer #(.select(3), .width(8)) multiplexer_1 (
    .in0(soma_8b_1_s), .in1(shift_r_1_d), .in2(shift_l_1_d), .in3(not_1_out), .in4(and_1_out), .in5(B),
    .in6(or_1_out), .in7(xor_1_out), .out(s), .sel(op));
  Multiplexer #(.select(3)) multiplexer_2 (
    .in0(soma_8b_1_c_out), .in1(shift_r_1_c_out), .in2(shift_l_1_c_out), .in3(1'b0), .in4(1'b0), .in5(1'b0),
    .in6(1'b0), .in7(1'b0), .out(c_out), .sel(op));
  and and_2 (and_2_out, ~b_1, c_in);  // AND_Gate
  nor nor_1 (zero, s[0], s[1], s[2], s[3], s[4], s[5], s[6], s[7]);
endmodule

module shift_r (
  input  [7:0] i,
  input  c_in,
  output [7:0] d,
  output c_out
);


  assign c_out = i[0];
  assign d = {c_in, i[7:1]};
endmodule

module shift_l (
  input  c_in,
  input  [7:0] i,
  output [7:0] d,
  output c_out
);


  assign c_out = i[7];
  assign d = {i[6:0], c_in};
endmodule

module comp_1b (
  input  iguais_ant,
  input  a_maior_ant,
  input  a,
  input  b,
  output c,
  output iguais,
  output a_maior
);

  wire and_2_out;

  xor xor_1 (c, a, b);
  and and_1 (iguais, ~c, iguais_ant);  // AND_Gate
  and and_2 (and_2_out, a, iguais_ant, c);
  or or_1 (a_maior, and_2_out, a_maior_ant);
endmodule

module comp_8b (
  input  [7:0] A,
  input  [7:0] B,
  output [7:0] C,
  output a_maior,
  output iguais
);

  wire comp_1b_1_a_maior, comp_1b_1_iguais, comp_1b_2_a_maior, comp_1b_2_iguais, comp_1b_3_a_maior,
       comp_1b_3_iguais, comp_1b_4_a_maior, comp_1b_4_iguais, comp_1b_5_a_maior, comp_1b_5_iguais,
       comp_1b_6_a_maior, comp_1b_6_iguais, comp_1b_7_a_maior, comp_1b_7_iguais;

  comp_1b comp_1b_1 (
    .a(A[0]), .b(B[0]), .iguais_ant(1'b1), .a_maior_ant(1'b0), .iguais(comp_1b_1_iguais),
    .a_maior(comp_1b_1_a_maior), .c(C[0]));
  comp_1b comp_1b_2 (
    .a(A[1]), .b(B[1]), .iguais_ant(comp_1b_1_iguais), .a_maior_ant(comp_1b_1_a_maior),
    .iguais(comp_1b_2_iguais), .a_maior(comp_1b_2_a_maior), .c(C[1]));
  comp_1b comp_1b_3 (
    .a(A[2]), .b(B[2]), .iguais_ant(comp_1b_2_iguais), .a_maior_ant(comp_1b_2_a_maior),
    .iguais(comp_1b_3_iguais), .a_maior(comp_1b_3_a_maior), .c(C[2]));
  comp_1b comp_1b_4 (
    .a(A[3]), .b(B[3]), .iguais_ant(comp_1b_3_iguais), .a_maior_ant(comp_1b_3_a_maior),
    .iguais(comp_1b_4_iguais), .a_maior(comp_1b_4_a_maior), .c(C[3]));
  comp_1b comp_1b_5 (
    .a(A[4]), .b(B[4]), .iguais_ant(comp_1b_4_iguais), .a_maior_ant(comp_1b_4_a_maior),
    .iguais(comp_1b_5_iguais), .a_maior(comp_1b_5_a_maior), .c(C[4]));
  comp_1b comp_1b_6 (
    .a(A[5]), .b(B[5]), .iguais_ant(comp_1b_5_iguais), .a_maior_ant(comp_1b_5_a_maior),
    .iguais(comp_1b_6_iguais), .a_maior(comp_1b_6_a_maior), .c(C[5]));
  comp_1b comp_1b_7 (
    .a(A[6]), .b(B[6]), .iguais_ant(comp_1b_6_iguais), .a_maior_ant(comp_1b_6_a_maior),
    .iguais(comp_1b_7_iguais), .a_maior(comp_1b_7_a_maior), .c(C[6]));
  comp_1b comp_1b_8 (
    .a(A[7]), .b(B[7]), .iguais_ant(comp_1b_7_iguais), .a_maior_ant(comp_1b_7_a_maior), .iguais(iguais),
    .a_maior(a_maior), .c(C[7]));
endmodule
